# Fritzing sketch ArduMacRemote (saved by Fritzing 0.9.0b)
circuit board: 2.54291cm x 2.05337cm
breadboards: 1

parts:
  U1 = attiny85 [package=dip]
  IR = RPM7100 [package=THT]
  LED = LED - 5mm [color="Red (633nm)" package="5 mm [THT]"]
  150R = Resistor [tolerance=±5% resistance=150 package=THT]
  USB = USB TTL [form="♀ (female)" package=THT]

nets:
  N1: U1.Pin_2, USB.RX
  N2: U1.Pin_3, LED.anode
  GND: U1.Pin_4, IR.GND, 150R.Pin_0, USB.GND
  N3: U1.Pin_6, IR.DATA
  VCC: U1.Pin_8, IR.VCC, USB.5V
  N4: LED.cathode, 150R.Pin_1

custom parts:
  RPM7100: Generic stand-in for RPM7100 IR receiver
  USB TTL: Generic stand-in for USB-TTL
